// Logisim project 16 bit computer.circ as structural Verilog
module CPU (
  output [7:0] out_1,
  output [7:0] out_2,
  output [7:0] out_3,
  output [7:0] out_4,
  output [7:0] out_5,
  output [7:0] out_6,
  output [7:0] out_7,
  output [7:0] out_8,
  output [7:0] out_9,
  output [7:0] out_10
);

  wire clock_1_out, jmp_a_out, mov_ah_value8_out, mov_al_value8_out, mov_ax_value16_out, mov_bh_value8_out,
       mov_bl_value8_out, mov_bx_value16_out, mov_ch_value8_out, mov_cl_value8_out, mov_cx_value16_out,
       mov_dh_value8_out, mov_dl_value8_out, mov_dx_value16_out, mov_sp_value16_out, mov_sph_value8_out,
       mov_spl_value8_out;
  wire [7:0] ram_1_data;
  wire [15:0] ip_register_small_1_ip;

  ip_Register_small ip_register_small_1 (
    .mov_ip_value16(jmp_a_out), .Data_In({out_1, out_2}), .CLK(clock_1_out), .ip(ip_register_small_1_ip));
  Clock clock_1 (.out(clock_1_out));
  RAM #(.addrWidth(16)) ram_1 (
    .addr(ip_register_small_1_ip), .data(ram_1_data), .clk(clock_1_out));  // open: sel, ld, clr
  and mov_ax_value16 (mov_ax_value16_out, ram_1_data[0], ~ram_1_data[1], ~ram_1_data[2], ~ram_1_data[3], ~ram_1_data[4], ~ram_1_data[5], ~ram_1_data[6], ~ram_1_data[7]);  // AND_Gate
  and mov_bx_value16 (mov_bx_value16_out, ~ram_1_data[0], ram_1_data[1], ~ram_1_data[2], ~ram_1_data[3], ~ram_1_data[4], ~ram_1_data[5], ~ram_1_data[6], ~ram_1_data[7]);  // AND_Gate
  and mov_cx_value16 (mov_cx_value16_out, ram_1_data[0], ram_1_data[1], ~ram_1_data[2], ~ram_1_data[3], ~ram_1_data[4], ~ram_1_data[5], ~ram_1_data[6], ~ram_1_data[7]);  // AND_Gate
  and mov_dx_value16 (mov_dx_value16_out, ~ram_1_data[0], ~ram_1_data[1], ram_1_data[2], ~ram_1_data[3], ~ram_1_data[4], ~ram_1_data[5], ~ram_1_data[6], ~ram_1_data[7]);  // AND_Gate
  and mov_sp_value16 (mov_sp_value16_out, ram_1_data[0], ~ram_1_data[1], ram_1_data[2], ~ram_1_data[3], ~ram_1_data[4], ~ram_1_data[5], ~ram_1_data[6], ~ram_1_data[7]);  // AND_Gate
  and mov_al_value8 (mov_al_value8_out, ~ram_1_data[0], ram_1_data[1], ram_1_data[2], ~ram_1_data[3], ~ram_1_data[4], ~ram_1_data[5], ~ram_1_data[6], ~ram_1_data[7]);  // AND_Gate
  and mov_ah_value8 (mov_ah_value8_out, ram_1_data[0], ram_1_data[1], ram_1_data[2], ~ram_1_data[3], ~ram_1_data[4], ~ram_1_data[5], ~ram_1_data[6], ~ram_1_data[7]);  // AND_Gate
  and mov_bl_value8 (mov_bl_value8_out, ~ram_1_data[0], ~ram_1_data[1], ~ram_1_data[2], ram_1_data[3], ~ram_1_data[4], ~ram_1_data[5], ~ram_1_data[6], ~ram_1_data[7]);  // AND_Gate
  and mov_bh_value8 (mov_bh_value8_out, ram_1_data[0], ~ram_1_data[1], ~ram_1_data[2], ram_1_data[3], ~ram_1_data[4], ~ram_1_data[5], ~ram_1_data[6], ~ram_1_data[7]);  // AND_Gate
  and mov_cl_value8 (mov_cl_value8_out, ~ram_1_data[0], ram_1_data[1], ~ram_1_data[2], ram_1_data[3], ~ram_1_data[4], ~ram_1_data[5], ~ram_1_data[6], ~ram_1_data[7]);  // AND_Gate
  and mov_ch_value8 (mov_ch_value8_out, ram_1_data[0], ram_1_data[1], ~ram_1_data[2], ram_1_data[3], ~ram_1_data[4], ~ram_1_data[5], ~ram_1_data[6], ~ram_1_data[7]);  // AND_Gate
  and mov_dl_value8 (mov_dl_value8_out, ~ram_1_data[0], ~ram_1_data[1], ram_1_data[2], ram_1_data[3], ~ram_1_data[4], ~ram_1_data[5], ~ram_1_data[6], ~ram_1_data[7]);  // AND_Gate
  and mov_dh_value8 (mov_dh_value8_out, ram_1_data[0], ~ram_1_data[1], ram_1_data[2], ram_1_data[3], ~ram_1_data[4], ~ram_1_data[5], ~ram_1_data[6], ~ram_1_data[7]);  // AND_Gate
  and mov_spl_value8 (mov_spl_value8_out, ~ram_1_data[0], ram_1_data[1], ram_1_data[2], ram_1_data[3], ~ram_1_data[4], ~ram_1_data[5], ~ram_1_data[6], ~ram_1_data[7]);  // AND_Gate
  and mov_sph_value8 (mov_sph_value8_out, ram_1_data[0], ram_1_data[1], ram_1_data[2], ram_1_data[3], ~ram_1_data[4], ~ram_1_data[5], ~ram_1_data[6], ~ram_1_data[7]);  // AND_Gate
  and jmp_a (jmp_a_out, ~ram_1_data[0], ~ram_1_data[1], ~ram_1_data[2], ~ram_1_data[3], ram_1_data[4], ~ram_1_data[5], ~ram_1_data[6], ~ram_1_data[7]);  // AND_Gate
  _16_Bit_Register ax (
    .mov_ax_value16(mov_ax_value16_out), .mov_ah_value8(mov_ah_value8_out),
    .mov_al_value8(mov_al_value8_out), .Data(ram_1_data), .CLK(clock_1_out), .ah(out_1), .al(out_2));
  _16_Bit_Register bx (
    .mov_ax_value16(mov_bx_value16_out), .mov_ah_value8(mov_bh_value8_out),
    .mov_al_value8(mov_bl_value8_out), .Data(ram_1_data), .CLK(clock_1_out), .ah(out_3), .al(out_4));
  _16_Bit_Register cx (
    .mov_ax_value16(mov_cx_value16_out), .mov_ah_value8(mov_ch_value8_out),
    .mov_al_value8(mov_cl_value8_out), .Data(ram_1_data), .CLK(clock_1_out), .ah(out_5), .al(out_6));
  _16_Bit_Register dx (
    .mov_ax_value16(mov_dx_value16_out), .mov_ah_value8(mov_dh_value8_out),
    .mov_al_value8(mov_dl_value8_out), .Data(ram_1_data), .CLK(clock_1_out), .ah(out_7), .al(out_8));
  _16_Bit_Register sp (
    .mov_ax_value16(mov_sp_value16_out), .mov_ah_value8(mov_sph_value8_out),
    .mov_al_value8(mov_spl_value8_out), .Data(ram_1_data), .CLK(clock_1_out), .ah(out_9), .al(out_10));
endmodule

module Register_small (
  input  mov_ah_value8,
  input  mov_al_value8,
  input  [7:0] Data_In,
  input  CLK,
  output [7:0] ah,
  output [7:0] al
);

  wire [7:0] transistor_1_out, transistor_2_out;

  Transistor #(.\type ("n"), .width(8)) transistor_1 (.in(Data_In), .out(transistor_1_out), .gate(mov_ah_value8));
  Transistor #(.\type ("n"), .width(8)) transistor_2 (.in(Data_In), .out(transistor_2_out), .gate(mov_al_value8));
  Register_part u_ah (.D(transistor_1_out), .en(mov_ah_value8), .Q(ah), .clk(CLK));  // open: clr
  Register_part u_al (.D(transistor_2_out), .en(mov_al_value8), .Q(al), .clk(CLK));  // open: clr
endmodule

module _2_cycle (
  input  Active,
  input  CLK,
  output Trigger
);

  wire and_1_out, d_ff_1_qn, or_1_out, t_ff_1_q;

  D_Flip_Flop d_ff_1 (
    .clk(CLK), .D(and_1_out), .Q(Trigger), .Qn(d_ff_1_qn), .en(or_1_out), .reset(t_ff_1_q));  // open: preset
  and and_1 (and_1_out, ~Trigger, Active);  // AND_Gate
  or or_1 (or_1_out, and_1_out, t_ff_1_q);
  T_Flip_Flop t_ff_1 (.clk(CLK), .T(Trigger), .Q(t_ff_1_q), .reset(d_ff_1_qn), .en(CLK));  // open: Qn, preset
endmodule

module _3_cycle (
  input  Active,
  input  CLK,
  output _1,
  output _2,
  output _3
);

  wire and_1_out, and_2_out, and_3_out, or_1_out;

  and and_1 (and_1_out, ~or_1_out, Active);  // AND_Gate
  D_Flip_Flop d_ff_1 (.clk(CLK), .D(and_2_out), .Q(_1));  // open: Qn, preset, en, reset
  and and_2 (and_2_out, ~_1, and_1_out);  // AND_Gate
  T_Flip_Flop t_ff_1 (.clk(CLK), .T(_1), .Q(_2), .reset(and_3_out), .en(CLK));  // open: Qn, preset
  and and_3 (and_3_out, _2, _3);
  or or_1 (or_1_out, _1, _2);
  D_Flip_Flop d_ff_2 (.clk(CLK), .D(_2), .Q(_3));  // open: Qn, preset, en, reset
endmodule

module _16_Bit_Register (
  input  mov_ax_value16,
  input  mov_ah_value8,
  input  mov_al_value8,
  input  [7:0] Data,
  input  CLK,
  output [7:0] ah,
  output [7:0] al
);

  wire n2_cycle_1_trigger, n2_cycle_2_trigger, n3_cycle_1__1, or_1_out, or_2_out, or_3_out;
  wire [7:0] transistor_1_out;

  or or_1 (or_1_out, mov_ax_value16, mov_ah_value8);
  or or_2 (or_2_out, n3_cycle_1__1, mov_al_value8);
  _3_cycle u_3_cycle_1 (.Active(mov_ax_value16), .CLK(CLK), ._1(n3_cycle_1__1));  // open: _2, _3
  _2_cycle u_2_cycle_1 (.Active(or_1_out), .CLK(CLK), .Trigger(n2_cycle_1_trigger));
  _2_cycle u_2_cycle_2 (.Active(or_2_out), .CLK(CLK), .Trigger(n2_cycle_2_trigger));
  or or_3 (or_3_out, n2_cycle_1_trigger, n2_cycle_2_trigger);
  Transistor #(.\type ("n"), .width(8)) transistor_1 (.in(Data), .out(transistor_1_out), .gate(or_3_out));
  Register_small ax (
    .mov_ah_value8(n2_cycle_1_trigger), .mov_al_value8(n2_cycle_2_trigger), .Data_In(transistor_1_out),
    .CLK(CLK), .ah(ah), .al(al));
endmodule

module ip_Register (
  input  mov_ip_value16,
  input  mov_iph_value8,
  input  mov_ipl_value8,
  input  [7:0] Data,
  input  CLK,
  output out_6,
  output [7:0] ah,
  output [7:0] al
);

  wire n2_cycle_1_trigger, n2_cycle_2_trigger, n3_cycle_1__1, or_1_out, or_2_out, or_3_out;
  wire [7:0] transistor_1_out;

  or or_1 (or_1_out, mov_ip_value16, mov_iph_value8);
  or or_2 (or_2_out, n3_cycle_1__1, mov_ipl_value8);
  _3_cycle u_3_cycle_1 (.Active(mov_ip_value16), .CLK(CLK), ._1(n3_cycle_1__1));  // open: _2, _3
  _2_cycle u_2_cycle_1 (.Active(or_1_out), .CLK(CLK), .Trigger(n2_cycle_1_trigger));
  _2_cycle u_2_cycle_2 (.Active(or_2_out), .CLK(CLK), .Trigger(n2_cycle_2_trigger));
  or or_3 (or_3_out, n2_cycle_1_trigger, n2_cycle_2_trigger);
  Transistor #(.\type ("n"), .width(8)) transistor_1 (.in(Data), .out(transistor_1_out), .gate(or_3_out));
  or or_4 (out_6, n2_cycle_2_trigger, n2_cycle_1_trigger);
  Register_small ax (
    .mov_ah_value8(n2_cycle_1_trigger), .mov_al_value8(n2_cycle_2_trigger), .Data_In(transistor_1_out),
    .CLK(CLK), .ah(ah), .al(al));
endmodule

module ip_Register_small (
  input  mov_ip_value16,
  input  [15:0] Data_In,
  input  CLK,
  output [15:0] ip
);

  wire not_1_out;

  not not_1 (not_1_out, mov_ip_value16);
  Counter #(.width(16), .max('hffff), .trigger("falling")) counter_1 (
    .load(mov_ip_value16), .D(Data_In), .count(not_1_out), .Q(ip), .clk(CLK));  // open: carry, clr
endmodule

module Register_Block (
);

  Register_small ax ();  // open: mov_ah_value8, mov_al_value8, Data_In, CLK, ah, al
  Register_small bx ();  // open: mov_ah_value8, mov_al_value8, Data_In, CLK, ah, al
  Register_small cx ();  // open: mov_ah_value8, mov_al_value8, Data_In, CLK, ah, al
  Register_small dx ();  // open: mov_ah_value8, mov_al_value8, Data_In, CLK, ah, al
  Register_small sp ();  // open: mov_ah_value8, mov_al_value8, Data_In, CLK, ah, al
endmodule

module Register (
  input  mov_reg_value16,
  input  mov_highbyte_value8,
  input  mov_lowbyte_value8,
  input  [7:0] value8_in,
  input  [15:0] value16_in,
  input  CLK,
  output [15:0] value16,
  output [7:0] High_Byte,
  output [7:0] Low_Byte
);

  wire or_1_out, or_2_out;
  wire [7:0] or_3_out, or_4_out, transistor_2_out;
  wire [15:0] transistor_1_out;

  Transistor #(.\type ("n"), .width(16)) transistor_1 (.in(value16_in), .out(transistor_1_out), .gate(mov_reg_value16));
  Transistor #(.width(8)) transistor_2 (.in(value8_in), .out(transistor_2_out), .gate(mov_reg_value16));
  or or_1 (or_1_out, mov_reg_value16, mov_lowbyte_value8);
  or or_2 (or_2_out, mov_reg_value16, mov_highbyte_value8);
  assign or_3_out = transistor_2_out | transistor_1_out[7:0];  // OR_Gate or_3, 8 bits wide
  assign or_4_out = transistor_2_out | transistor_1_out[15:8];  // OR_Gate or_4, 8 bits wide
  Register_part u_low_byte (.D(or_3_out), .en(or_1_out), .Q(Low_Byte), .clk(CLK));  // open: clr
  Register_part u_high_byte (.D(or_4_out), .en(or_2_out), .Q(High_Byte), .clk(CLK));  // open: clr

  assign value16 = {High_Byte, Low_Byte};
endmodule

module RegisterPlusAnd (
  input  CLK,
  input  d0,
  input  in_3,
  input  in_4,
  input  in_5,
  input  in_6,
  input  in_7,
  input  in_8,
  input  d7,
  output [7:0] out_10,
  output [7:0] out_11,
  output [7:0] out_12,
  output [7:0] out_13,
  output [7:0] out_14,
  output [7:0] out_15,
  output [7:0] out_16,
  output [7:0] out_17,
  output [7:0] out_18,
  output [7:0] out_19
);

  _16_Bit_Register ax (
    .Data({d7, in_8, in_7, in_6, in_5, in_4, in_3, d0}), .CLK(CLK), .ah(out_10), .al(out_11));  // open: mov_ax_value16, mov_ah_value8, mov_al_value8
  _16_Bit_Register bx (
    .Data({d7, in_8, in_7, in_6, in_5, in_4, in_3, d0}), .CLK(CLK), .ah(out_12), .al(out_13));  // open: mov_ax_value16, mov_ah_value8, mov_al_value8
  _16_Bit_Register cx (
    .Data({d7, in_8, in_7, in_6, in_5, in_4, in_3, d0}), .CLK(CLK), .ah(out_14), .al(out_15));  // open: mov_ax_value16, mov_ah_value8, mov_al_value8
  _16_Bit_Register dx (
    .Data({d7, in_8, in_7, in_6, in_5, in_4, in_3, d0}), .CLK(CLK), .ah(out_16), .al(out_17));  // open: mov_ax_value16, mov_ah_value8, mov_al_value8
  _16_Bit_Register sp (
    .Data({d7, in_8, in_7, in_6, in_5, in_4, in_3, d0}), .CLK(CLK), .ah(out_18), .al(out_19));  // open: mov_ax_value16, mov_ah_value8, mov_al_value8
endmodule

module _16_bit_Reg (
  input  CLK,
  input  mov_reg_value16,
  input  mov_regh_value8,
  input  mov_regl_value8,
  input  [7:0] Data,
  output reg_write,
  output [7:0] regh,
  output [7:0] regl
);

  wire d_ff_1_q, d_ff_2_q, d_ff_3_q, d_ff_4_q, or_1_out, or_3_out;

  D_Flip_Flop d_ff_1 (.clk(CLK), .D(mov_regh_value8), .Q(d_ff_1_q));  // open: Qn, preset, en, reset
  D_Flip_Flop d_ff_2 (.clk(CLK), .D(mov_regl_value8), .Q(d_ff_2_q));  // open: Qn, preset, en, reset
  D_Flip_Flop d_ff_3 (.clk(CLK), .D(mov_reg_value16), .Q(d_ff_3_q));  // open: Qn, preset, en, reset
  or or_1 (or_1_out, d_ff_3_q, d_ff_2_q);
  D_Flip_Flop d_ff_4 (.clk(CLK), .D(d_ff_3_q), .Q(d_ff_4_q));  // open: Qn, preset, en, reset
  or or_2 (reg_write, or_1_out, or_3_out);
  or or_3 (or_3_out, d_ff_4_q, d_ff_1_q);
  Register_part u_regh (.D(Data), .en(or_3_out), .Q(regh), .clk(CLK));  // open: clr
  Register_part u_regl (.D(Data), .en(or_1_out), .Q(regl), .clk(CLK));  // open: clr
endmodule

module CPU_2 (
  input  write,
  input  [7:0] in_2,
  input  in_3,
  input  in_4,
  input  [15:0] in_5,
  input  in_6,
  input  enable,
  input  in_8,
  input  in_9,
  input  [7:0] in_10,
  input  [7:0] in_11,
  output [7:0] out_12,
  output [7:0] out_13,
  output [7:0] out_14,
  output [7:0] out_15,
  output [7:0] out_16,
  output [7:0] out_17,
  output [7:0] out_18,
  output [7:0] out_19,
  output [7:0] out_20,
  output [7:0] out_21,
  output [7:0] out_22
);

  wire clock_1_out, counter_2_carry, counter_3_carry, counter_4_carry, d_ff_1_q, decoder_1_mov_ax_value16,
       decoder_1_mov_bx_value16, or_2_out, undriven, undriven_2, undriven_3, undriven_4, undriven_5,
       undriven_6;
  wire [7:0] counter_2_q, counter_3_q, counter_4_q, decoder_1_data_out, or_1_out;
  wire [15:0] counter_1_q;

  Clock clock_1 (.out(clock_1_out));
  Counter #(.width(16), .max('hffff)) counter_1 (
    .load(in_3), .D(in_5), .count(in_6), .Q(counter_1_q), .clk(clock_1_out));  // open: carry, clr
  assign or_1_out = in_11 | in_11;  // OR_Gate or_1, 8 bits wide
  RAM #(.addrWidth(16), .bus("separate")) ram_1 (
    .addr(counter_1_q), .din(or_1_out), .data(in_2), .str(in_8), .sel(enable), .clk(clock_1_out), .ld(in_9));  // open: clr
  Decoder decoder_1 (
    .CLK(clock_1_out), .data_in(in_10), .data_out(decoder_1_data_out),
    .mov_ax_value16(decoder_1_mov_ax_value16), .mov_bx_value16(decoder_1_mov_bx_value16));  // open: mov_cx_value16, mov_dx_value16, mov_dx_value16_2
  Counter counter_2 (
    .load(undriven), .D(in_2), .count(undriven_2), .Q(counter_2_q), .carry(counter_2_carry), .clk(write));  // open: clr
  Counter counter_3 (
    .load(undriven_3), .D(in_2), .count(undriven_4), .Q(counter_3_q), .carry(counter_3_carry), .clk(write));  // open: clr
  Counter counter_4 (
    .load(undriven_5), .D(in_2), .count(undriven_6), .Q(counter_4_q), .carry(counter_4_carry), .clk(write));  // open: clr
  or or_2 (or_2_out, in_4, in_4);
  _16_bit_Reg ax (
    .CLK(clock_1_out), .mov_reg_value16(decoder_1_mov_ax_value16), .Data(decoder_1_data_out), .regh(out_13),
    .regl(out_14));  // open: mov_regh_value8, mov_regl_value8, reg_write
  _16_bit_Reg bx (
    .CLK(clock_1_out), .mov_reg_value16(decoder_1_mov_bx_value16), .Data(decoder_1_data_out), .regh(out_15),
    .regl(out_16));  // open: mov_regh_value8, mov_regl_value8, reg_write
  _16_bit_Reg cx (
    .regh(out_17), .regl(out_18));  // open: CLK, mov_reg_value16, mov_regh_value8, mov_regl_value8, Data, reg_write
  _16_bit_Reg dx (
    .regh(out_19), .regl(out_20));  // open: CLK, mov_reg_value16, mov_regh_value8, mov_regl_value8, Data, reg_write
  _16_bit_Reg sp (
    .regh(out_21), .regl(out_22));  // open: CLK, mov_reg_value16, mov_regh_value8, mov_regl_value8, Data, reg_write
  D_Flip_Flop d_ff_1 (.clk(clock_1_out), .D(or_2_out), .Q(d_ff_1_q));  // open: Qn, preset, en, reset
  RAM #(.addrWidth(24), .bus("separate")) ram_2 (
    .addr({counter_4_q, counter_3_q, counter_2_q}), .sel(d_ff_1_q), .clk(clock_1_out));  // open: din, data, str, ld, clr

  assign out_12 = in_2;

  // Notes on the sheet:
  //   Program execute/program read write memory
  //   24 bit memory for graphics
endmodule

module RAM_Interface (
  input  CLK,
  input  load,
  input  store,
  input  [7:0] data_in,
  output [7:0] data_out
);

  Counter #(.width(16), .max('hffff)) counter_1 ();  // open: load, D, count, Q, carry, clk, clr
  RAM #(.addrWidth(16), .bus("separate")) ram_1 (.clk(CLK));  // open: addr, din, data, str, sel, ld, clr
endmodule

module Decoder (
  input  CLK,
  input  [7:0] data_in,
  output [7:0] data_out,
  output mov_ax_value16,
  output mov_bx_value16,
  output mov_cx_value16,
  output mov_dx_value16,
  output mov_dx_value16_2
);

  wire and_1_out, exec_q, mov_ax_value16_out, mov_bx_value16_out, mov_cx_value16_out, mov_dx_value16_out,
       mov_sp_value16_out, n3_cycle_1__1, n3_cycle_1__2, n3_cycle_1__3, or_1_out, or_2_out;

  and u_mov_ax_value16 (mov_ax_value16_out, data_in[0], ~data_in[1], ~data_in[2], ~data_in[3], ~data_in[4], ~data_in[5], ~data_in[6], ~data_in[7]);  // AND_Gate
  and u_mov_bx_value16 (mov_bx_value16_out, ~data_in[0], data_in[1], ~data_in[2], ~data_in[3], ~data_in[4], ~data_in[5], ~data_in[6], ~data_in[7]);  // AND_Gate
  and u_mov_cx_value16 (mov_cx_value16_out, data_in[0], data_in[1], ~data_in[2], ~data_in[3], ~data_in[4], ~data_in[5], ~data_in[6], ~data_in[7]);  // AND_Gate
  and u_mov_dx_value16 (mov_dx_value16_out, ~data_in[0], ~data_in[1], data_in[2], ~data_in[3], ~data_in[4], ~data_in[5], ~data_in[6], ~data_in[7]);  // AND_Gate
  and mov_sp_value16 (mov_sp_value16_out, data_in[0], ~data_in[1], data_in[2], ~data_in[3], ~data_in[4], ~data_in[5], ~data_in[6], ~data_in[7]);  // AND_Gate
  D_Flip_Flop #(.trigger("high")) exec (.clk(CLK), .D(or_2_out), .Q(exec_q));  // open: Qn, preset, en, reset
  and and_1 (and_1_out, or_1_out, ~n3_cycle_1__1, ~n3_cycle_1__2, ~1'b0);  // AND_Gate
  or or_1 (or_1_out, mov_ax_value16_out, mov_bx_value16_out, mov_cx_value16_out, mov_dx_value16_out, mov_sp_value16_out);
  _3_cycle u_3_cycle_1 (.Active(and_1_out), .CLK(CLK), ._1(n3_cycle_1__1), ._2(n3_cycle_1__2), ._3(n3_cycle_1__3));
  or or_2 (or_2_out, n3_cycle_1__1, n3_cycle_1__2);
  and and_2 (mov_ax_value16, ~exec_q, mov_ax_value16_out);  // AND_Gate
  and and_3 (mov_bx_value16, ~exec_q, mov_bx_value16_out);  // AND_Gate
  and and_4 (mov_cx_value16, ~exec_q, mov_cx_value16_out);  // AND_Gate
  and and_5 (mov_dx_value16, ~exec_q, mov_dx_value16_out);  // AND_Gate
  and and_6 (mov_dx_value16_2, ~exec_q, mov_sp_value16_out);  // AND_Gate

  assign data_out = data_in;
endmodule
